# Fritzing sketch circuit (saved by Fritzing 0.9.3b)
circuit board: 8.46667cm x 5.64444cm

parts:
  Arduino = Arduino Nano (Rev3.0)
  Bluetooth = Bluetooth HC-06u [package=THT]
  LED_Strip_2 = Neopixel Strip -- Black (60/m) [part_number=1461]
  LED_Strip_1 = Neopixel Strip -- Black (60/m) [part_number=1461]

nets:
  GND: Arduino.GND, Bluetooth.GND, LED_Strip_1.GND#3
  N1: Arduino.D2, LED_Strip_1.DI
  N2: Arduino.D3, LED_Strip_2.DI
  N3: Arduino.D8, Bluetooth.RXD
  N4: Arduino.D9, Bluetooth.TXD
  N5: Arduino.VIN, LED_Strip_1.+5V#1
  5V: Arduino.5V, Bluetooth.VCC
  N6: LED_Strip_2.GND, LED_Strip_1.GND#4
  N7: LED_Strip_2.+5V, LED_Strip_1.+5V#6

custom parts:
  Bluetooth HC-06u: Bluetooth HC-06 - face up, pins down 16.5mm x 37.5mm PCB
  Neopixel Strip -- Black (60/m): Neopixel Strip, Black, 60 pixels per meter.
